# Fritzing sketch blinkers-and-brakes-ii (saved by Fritzing 0.9.3b)
perfboards: 2

parts:
  C2 = Electrolytic Capacitor [capacitance=1µF package="100 mil [THT, electrolytic]"]
  C3 = Ceramic Capacitor [capacitance=100nF package="100 mil [THT, multilayer]"]
  U1 = 555 Timer [package="DIP8 [THT]"]
  R3 = Resistor [tolerance=±5% resistance=470 package=THT]
  R4 = Resistor [tolerance=±5% resistance=470k package=THT]
  R5 = Resistor [tolerance=±5% resistance=470 package=THT]
  LED2 = LED - 3mm [color="Orange (620nm)" package="3 mm [THT]"]
  LED3 = LED - 3mm [color="Orange (620nm)" package="3 mm [THT]"]
  Q2 = NPN-Transistor [package="TO92 [THT]"]
  Q3 = NPN-Transistor [package="TO92 [THT]"]
  LED4 = LED - 3mm [color="Red (633nm)" package="3 mm [THT]"]
  LED5 = LED - 3mm [color="Red (633nm)" package="3 mm [THT]"]
  R6 = Resistor [tolerance=±5% resistance=10k package=THT]
  R7 = Resistor [tolerance=±5% resistance=10k package=THT]
  R8 = Resistor [tolerance=±5% resistance=470 package=THT]
  J1 = female pin header, 5 pins [form="♀ (female)"]
  Q4 = NPN-Transistor [package="TO92 [THT]"]
  R9 = Resistor [tolerance=±5% resistance=10k package=THT]
  J2 = female pin header, 4 pins [form="♀ (female)"]
  J3 = female pin header, 4 pins [form="♀ (female)"]
  U2 = 555 Timer [package="DIP8 [THT]"]
  J5 = female pin header, 4 pins [form="♀ (female)"]  # not connected
  J6 = female pin header, 4 pins [form="♀ (female)"]  # not connected
  J7 = female pin header, 5 pins [form="♀ (female)"]  # not connected

nets:
  N1: C2.+, Q4.C
  N2: C3.0, U1.Control_Voltage
  N3: U1.Ground, Q2.C
  N4: U1.Trigger, U1.Threshold
  N5: U1.Output, R5.Pin_1
  N6: U1.Discharge, R4.Pin_0
  N7: R3.Pin_0, R8.Pin_1, J1.pin4
  N8: R5.Pin_0, LED2.anode, LED3.anode, J2.pin4, J3.pin4
  N9: LED2.cathode, Q3.E, J3.pin3
  N10: LED3.cathode, Q2.E, J2.pin3
  N11: Q2.B, R6.Pin_1
  N12: Q3.B, R7.Pin_1
  N13: LED4.cathode, LED5.anode, J2.pin2, J3.pin2
  N14: LED5.cathode, Q4.E, J3.pin1
  N15: R6.Pin_0, J1.pin1
  N16: R7.Pin_0, J1.pin2
  N17: R8.Pin_0, J2.pin1
  N18: J1.pin3, R9.Pin_1
  N19: Q4.B, R9.Pin_0
  N20: U2.Trigger, U2.Threshold
